// Digital circuit 4bit-computer-full.dig as structural Verilog
module _4bit_computer_full (
  input  Auto_Manual,
  input  Reset,
  input  Bus,
  input  Flags,
  input  Clock,
  input  Minus,
  input  Reset_2,
  input  Read,
  input  Clock_2,
  input  Reset_3,
  input  Read_2,
  input  Clock_3,
  input  _24,
  input  _20,
  input  _18,
  input  _17,
  input  Reset_4,
  input  Read_3,
  input  Clock_4,
  input  Bus_2,
  input  Save,
  input  Reset_5,
  input  Read_4,
  input  Clock_5,
  input  Reset_6,
  input  Clock_6,
  input  Write,
  input  Read_E,
  input  Read_B,
  input  in_50,
  input  in_51,
  input  in_52,
  input  in_53,
  output _1,
  output _2,
  output _3,
  output _4,
  output _5,
  output _6,
  output _7,
  output _8,
  output _9,
  output _10,
  output _11,
  output _12,
  output _13,
  output _14,
  output _15,
  output _16,
  output Out_24,
  output Out_20,
  output Out_18,
  output Out_17
);

  wire _7404_1_pin8, _7404_2_pin8, _7404_2_pin10, _7404_4_pin8, _7408_1_pin1, _7408_1_pin3, _7408_1_pin4,
       _7408_1_pin6, _7408_1_pin8, _7408_1_pin9, _7408_1_pin11, _7408_1_pin12, _7432_1_pin1, _7432_1_pin4,
       _7432_1_pin9, _7432_1_pin12, _74173_2_pin11, _74173_2_pin12, _74173_2_pin13, _74173_2_pin14,
       _74173_4_pin9, _74173_5_pin9, adapted_28c16a_1_p18, adapted_28c16a_1_p20, adapted_28c16a_1_p21,
       AND_pin3, BUS_pin6, BUS_pin7, BUS_pin8, BUS_pin9, BUS_pin19, NOR_pin1, NOR_pin4, NOR_pin10,
       NOT_2_pin4, NOT_2_pin6, NOT_2_pin8, NOT_2_pin10, NOT_2_pin12, NOT_pin4, NOT_pin6, NOT_pin10,
       NOT_pin12, RAM_2_pin5, RAM_2_pin7, RAM_2_pin9, RAM_2_pin11, RAM_2_pin12, RAM_pin1, RAM_pin3, RAM_pin4,
       RAM_pin5, RAM_pin6, RAM_pin7, RAM_pin9, RAM_pin10, RAM_pin11, RAM_pin12, RAM_pin13, RAM_pin14,
       RAM_pin15, Register_pin3, Register_pin4, SUM_2_pin3, SUM_2_pin5, SUM_2_pin12, SUM_2_pin14, SUM_pin1,
       SUM_pin3, SUM_pin4, SUM_pin5, SUM_pin10, SUM_pin12, SUM_pin13, SUM_pin14, XOR_pin1, XOR_pin4,
       XOR_pin9, XOR_pin12;

  _7404 _7404_1 (
    .pin1(1'b0), .pin3(1'b0), .pin5(1'b0), .pin7(1'b0), .pin8(_7404_1_pin8), .pin9(Read_4), .pin11(1'b0),
    .pin13(1'b0), .pin14(1'b1));  // open: pin2, pin4, pin6, pin10, pin12
  _7408 _7408_1 (
    .pin1(_7408_1_pin1), .pin2(_7404_1_pin8), .pin3(_7408_1_pin3), .pin4(_7408_1_pin4), .pin5(_7404_1_pin8),
    .pin6(_7408_1_pin6), .pin7(1'b0), .pin8(_7408_1_pin8), .pin9(_7408_1_pin9), .pin10(_7404_1_pin8),
    .pin11(_7408_1_pin11), .pin12(_7408_1_pin12), .pin13(_7404_1_pin8), .pin14(1'b1));
  _7404 _7404_2 (
    .pin1(1'b0), .pin3(1'b0), .pin5(1'b0), .pin7(1'b0), .pin8(_7404_2_pin8), .pin9(Read_E),
    .pin10(_7404_2_pin10), .pin11(Read_B), .pin13(1'b0), .pin14(1'b1));  // open: pin2, pin4, pin6, pin12
  _74189 RAM (
    .pin1(RAM_pin1), .pin2(1'b0), .pin3(RAM_pin3), .pin4(RAM_pin4), .pin5(RAM_pin5), .pin6(RAM_pin6),
    .pin7(RAM_pin7), .pin8(1'b0), .pin9(RAM_pin9), .pin10(RAM_pin10), .pin11(RAM_pin11), .pin12(RAM_pin12),
    .pin13(RAM_pin13), .pin14(RAM_pin14), .pin15(RAM_pin15), .pin16(1'b1));
  _74283 _74283_1 (
    .pin1(_7408_1_pin4), .pin2(1'b0), .pin3(RAM_pin14), .pin4(_7408_1_pin1), .pin5(RAM_pin13), .pin6(1'b1),
    .pin7(1'b0), .pin8(1'b0), .pin10(_7408_1_pin12), .pin11(1'b0), .pin12(RAM_pin1), .pin13(_7408_1_pin9),
    .pin14(RAM_pin15), .pin15(1'b0), .pin16(1'b1));  // open: pin9
  _74173 _74173_1 (
    .pin1(Write), .pin2(Write), .pin3(RAM_pin12), .pin4(RAM_pin10), .pin5(RAM_pin6), .pin6(RAM_pin4),
    .pin7(Clock_6), .pin8(1'b0), .pin9(_7404_2_pin8), .pin10(_7404_2_pin8), .pin11(in_50), .pin12(in_51),
    .pin13(in_52), .pin14(in_53), .pin15(Reset_6), .pin16(1'b1));
  Adapted_28C16A_V2 adapted_28c16a_v2_1 (
    .A0(Register_pin3), .A1(Register_pin4), .A2(NOT_pin10), .A3(NOT_pin12), .nCE(Auto_Manual), .nOE(1'b1),
    .nWE(1'b0), .VCC(1'b1), .GND(1'b0), .I_O0(_1), .I_O1(_2), .I_O2(_3), .I_O3(_4), .I_O4(_5), .I_O5(_6),
    .I_O6(_7), .I_O7(_8), .A4(NOT_pin4), .A5(NOT_pin6));
  _7404 NOT (
    .pin1(1'b0), .pin3(RAM_pin7), .pin4(NOT_pin4), .pin5(RAM_pin5), .pin6(NOT_pin6), .pin7(1'b0),
    .pin8(RAM_pin3), .pin9(Save), .pin10(NOT_pin10), .pin11(RAM_pin11), .pin12(NOT_pin12), .pin13(RAM_pin9),
    .pin14(1'b1));  // open: pin2
  _74173 _74173_2 (
    .pin1(1'b0), .pin2(1'b0), .pin3(RAM_pin1), .pin4(RAM_pin15), .pin5(RAM_pin14), .pin6(RAM_pin13),
    .pin7(Clock_5), .pin8(1'b0), .pin9(1'b0), .pin10(1'b0), .pin11(_74173_2_pin11), .pin12(_74173_2_pin12),
    .pin13(_74173_2_pin13), .pin14(_74173_2_pin14), .pin15(Reset_5), .pin16(1'b1));
  // Adapted_28C16A adapted_28c16a_1: pin names not known; wires that end beside it: 1'b1, 1'b0, 1'b0, 1'b0, 1'b0, 1'b0, 1'b0, 1'b0, 1'b1, RAM_pin1, 1'b0, RAM_pin15, Write, RAM_pin14, RAM_pin12, RAM_pin13, RAM_pin10, adapted_28c16a_1_p18, RAM_pin6, adapted_28c16a_1_p20, adapted_28c16a_1_p21, 1'b0
  Adapted_28C16A_V2 adapted_28c16a_v2_2 (
    .A0(Register_pin3), .A1(Register_pin4), .A2(NOT_pin10), .A3(NOT_pin12), .nCE(Auto_Manual), .nOE(1'b1),
    .nWE(1'b0), .VCC(1'b1), .GND(1'b0), .I_O0(_9), .I_O1(_10), .I_O2(_11), .I_O3(_12), .I_O4(_13),
    .I_O5(_14), .I_O6(_15), .I_O7(_16), .A4(NOT_pin4), .A5(NOT_pin6));
  _74189 RAM_2 (
    .pin1(RAM_pin1), .pin2(1'b0), .pin3(RAM_pin3), .pin4(adapted_28c16a_1_p18), .pin5(RAM_2_pin5),
    .pin6(adapted_28c16a_1_p20), .pin7(RAM_2_pin7), .pin8(1'b0), .pin9(RAM_2_pin9),
    .pin10(adapted_28c16a_1_p21), .pin11(RAM_2_pin11), .pin12(RAM_2_pin12), .pin13(RAM_pin13),
    .pin14(RAM_pin14), .pin15(RAM_pin15), .pin16(1'b1));
  _7432 _7432_1 (
    .pin1(_7432_1_pin1), .pin2(_7408_1_pin3), .pin3(_74173_2_pin14), .pin4(_7432_1_pin4),
    .pin5(_7408_1_pin6), .pin6(_74173_2_pin13), .pin7(1'b0), .pin8(_74173_2_pin12), .pin9(_7432_1_pin9),
    .pin10(_7408_1_pin8), .pin11(_74173_2_pin11), .pin12(_7432_1_pin12), .pin13(_7408_1_pin11), .pin14(1'b1));
  _7404 NOT_2 (
    .pin1(1'b0), .pin3(RAM_2_pin7), .pin4(NOT_2_pin4), .pin5(RAM_2_pin5), .pin6(NOT_2_pin6), .pin7(1'b0),
    .pin8(NOT_2_pin8), .pin9(Bus_2), .pin10(NOT_2_pin10), .pin11(RAM_2_pin11), .pin12(NOT_2_pin12),
    .pin13(RAM_2_pin9), .pin14(1'b1));  // open: pin2
  _74173 _74173_3 (
    .pin1(Write), .pin2(Write), .pin3(RAM_2_pin12), .pin4(adapted_28c16a_1_p21), .pin5(adapted_28c16a_1_p20),
    .pin6(adapted_28c16a_1_p18), .pin7(Clock_6), .pin8(1'b0), .pin9(_7404_2_pin10), .pin10(_7404_2_pin10),
    .pin11(in_50), .pin12(in_51), .pin13(in_52), .pin14(in_53), .pin15(Reset_6), .pin16(1'b1));
  _7408 _7408_2 (
    .pin1(in_53), .pin2(Read_4), .pin3(_7432_1_pin1), .pin4(in_52), .pin5(Read_4), .pin6(_7432_1_pin4),
    .pin7(1'b0), .pin8(_7432_1_pin9), .pin9(in_51), .pin10(Read_4), .pin11(_7432_1_pin12), .pin12(in_50),
    .pin13(Read_4), .pin14(1'b1));
  _74245 \_3_state__кранче  (
    .pin1(1'b1), .pin2(NOT_2_pin6), .pin3(NOT_2_pin4), .pin4(NOT_2_pin12), .pin5(NOT_2_pin10), .pin6(1'b0),
    .pin7(1'b0), .pin8(1'b0), .pin9(1'b0), .pin10(1'b0), .pin15(in_50), .pin16(in_51), .pin17(in_52),
    .pin18(in_53), .pin19(NOT_2_pin8), .pin20(1'b1));  // open: pin11, pin12, pin13, pin14
  PullDown pulldown_1 (.out(in_50));
  PullDown pulldown_2 (.out(in_51));
  PullDown pulldown_3 (.out(in_52));
  PullDown pulldown_4 (.out(in_53));
  _74245 u_BUS (
    .pin1(1'b1), .pin2(1'b0), .pin3(1'b0), .pin4(1'b0), .pin5(1'b0), .pin6(BUS_pin6), .pin7(BUS_pin7),
    .pin8(BUS_pin8), .pin9(BUS_pin9), .pin10(1'b0), .pin11(in_53), .pin12(in_52), .pin13(in_51),
    .pin14(in_50), .pin19(BUS_pin19), .pin20(1'b1));  // open: pin15, pin16, pin17, pin18
  _74283 SUM (
    .pin1(SUM_pin1), .pin2(1'b0), .pin3(SUM_pin3), .pin4(SUM_pin4), .pin5(SUM_pin5), .pin6(1'b0),
    .pin7(Minus), .pin8(1'b0), .pin10(SUM_pin10), .pin11(1'b0), .pin12(SUM_pin12), .pin13(SUM_pin13),
    .pin14(SUM_pin14), .pin15(1'b0), .pin16(1'b1));  // open: pin9
  _74173 _74173_4 (
    .pin1(1'b0), .pin2(1'b0), .pin3(Out_24), .pin4(Out_20), .pin5(Out_18), .pin6(Out_17), .pin7(Clock_4),
    .pin8(1'b0), .pin9(_74173_4_pin9), .pin10(_74173_4_pin9), .pin11(_17), .pin12(_18), .pin13(_20),
    .pin14(_24), .pin15(Reset_4), .pin16(1'b1));
  LED led_1 (.in(Out_24));
  LED led_2 (.in(Out_20));
  LED led_3 (.in(Out_18));
  LED led_4 (.in(Out_17));
  _7404 _7404_3 (
    .pin1(1'b0), .pin3(1'b0), .pin5(1'b0), .pin7(1'b0), .pin8(_74173_4_pin9), .pin9(Read_3), .pin11(1'b0),
    .pin13(1'b0), .pin14(1'b1));  // open: pin2, pin4, pin6, pin10, pin12
  _74283 SUM_2 (
    .pin1(BUS_pin8), .pin2(SUM_pin1), .pin3(SUM_2_pin3), .pin4(BUS_pin9), .pin5(SUM_2_pin5), .pin6(SUM_pin4),
    .pin7(1'b0), .pin8(1'b0), .pin10(BUS_pin6), .pin11(SUM_pin10), .pin12(SUM_2_pin12), .pin13(BUS_pin7),
    .pin14(SUM_2_pin14), .pin15(SUM_pin13), .pin16(1'b1));  // open: pin9
  _7486 XOR (
    .pin1(XOR_pin1), .pin2(Minus), .pin3(SUM_pin5), .pin4(XOR_pin4), .pin5(Minus), .pin6(SUM_pin3),
    .pin7(1'b0), .pin8(SUM_pin14), .pin9(XOR_pin9), .pin10(Minus), .pin11(SUM_pin12), .pin12(XOR_pin12),
    .pin13(Minus), .pin14(1'b1));
  _74173 _74173_5 (
    .pin1(1'b0), .pin2(1'b0), .pin3(SUM_2_pin5), .pin4(SUM_2_pin3), .pin5(SUM_2_pin14), .pin6(SUM_2_pin12),
    .pin7(Clock_3), .pin8(1'b0), .pin9(_74173_5_pin9), .pin10(_74173_5_pin9), .pin11(in_50), .pin12(in_51),
    .pin13(in_52), .pin14(in_53), .pin15(Reset_3), .pin16(1'b1));
  _7404 _7404_4 (
    .pin1(1'b0), .pin3(1'b0), .pin5(1'b0), .pin7(1'b0), .pin8(_7404_4_pin8), .pin9(Read), .pin11(1'b0),
    .pin13(1'b0), .pin14(1'b1));  // open: pin2, pin4, pin6, pin10, pin12
  LED led_5 (.in(SUM_2_pin5));
  LED led_6 (.in(SUM_2_pin3));
  LED led_7 (.in(SUM_2_pin14));
  LED led_8 (.in(SUM_2_pin12));
  _7404 _7404_5 (
    .pin1(1'b0), .pin3(1'b0), .pin5(1'b0), .pin7(1'b0), .pin8(_74173_5_pin9), .pin9(Read_2), .pin11(1'b0),
    .pin13(1'b0), .pin14(1'b1));  // open: pin2, pin4, pin6, pin10, pin12
  LED led_9 (.in(XOR_pin12));
  LED led_10 (.in(XOR_pin9));
  LED led_11 (.in(XOR_pin4));
  LED led_12 (.in(XOR_pin1));
  _74173 _74173_6 (
    .pin1(1'b0), .pin2(1'b0), .pin3(XOR_pin1), .pin4(XOR_pin4), .pin5(XOR_pin9), .pin6(XOR_pin12),
    .pin7(Clock_2), .pin8(1'b0), .pin9(_7404_4_pin8), .pin10(_7404_4_pin8), .pin11(in_50), .pin12(in_51),
    .pin13(in_52), .pin14(in_53), .pin15(Reset_2), .pin16(1'b1));
  LED led_13 (.in(BUS_pin7));
  LED led_14 (.in(BUS_pin8));
  LED led_15 (.in(BUS_pin9));
  LED led_16 (.in(BUS_pin6));
  _7402 NOR (
    .pin1(NOR_pin1), .pin2(BUS_pin9), .pin3(BUS_pin8), .pin4(NOR_pin4), .pin5(BUS_pin7), .pin6(BUS_pin6),
    .pin7(1'b0), .pin8(Flags), .pin9(1'b0), .pin10(NOR_pin10), .pin11(Bus), .pin12(1'b0), .pin13(BUS_pin19),
    .pin14(1'b1));
  _7408 AND (
    .pin1(NOR_pin1), .pin2(NOR_pin4), .pin3(AND_pin3), .pin4(1'b0), .pin5(1'b0), .pin7(1'b0), .pin9(1'b0),
    .pin10(1'b0), .pin12(1'b0), .pin13(1'b0), .pin14(1'b1));  // open: pin6, pin8, pin11
  _74173 Register (
    .pin1(1'b0), .pin2(1'b0), .pin3(Register_pin3), .pin4(Register_pin4), .pin7(Clock), .pin8(1'b0),
    .pin9(NOR_pin10), .pin10(NOR_pin10), .pin11(1'b0), .pin12(1'b0), .pin13(AND_pin3), .pin14(BUS_pin6),
    .pin15(Reset), .pin16(1'b1));  // open: pin5, pin6

  // Notes on the sheet:
  //   First Board
  //   Third Board
  //   Second Board
endmodule
