// Digital circuit 4bit-computer.dig as structural Verilog
module _4bit_computer (
  input  _8,
  input  A_M,
  input  Start_Program,
  input  Read_Command_Argument,
  input  Read_Command,
  input  Write_to_rC,
  input  Reset,
  input  Clock,
  input  Write_to_rA,
  input  Write_to_rB,
  input  Write_to_RAM,
  input  RAM_to_Bus,
  input  APU_to_Bus,
  input  Flags,
  input  Minus,
  input  Read_Addresses,
  input  _4,
  input  _2,
  input  _1,
  input  rC_to_Bus
);

  wire address_register_1__1, address_register_1__2, address_register_1__4, address_register_1__8,
       instructions_1_p5, instructions_1_p6, ram_storage_1_out_1, ram_storage_1_out_2, ram_storage_1_out_4,
       ram_storage_1_out_8, register_1_out_1, register_1_out_2, register_1_out_4, register_1_out_8,
       register_2_out_1, register_2_out_2, register_2_out_4, register_2_out_8,
       registers_and_programmer_1_b_1, registers_and_programmer_1_b_2, registers_and_programmer_1_b_4,
       registers_and_programmer_1_b_8, registers_and_programmer_1_e_1, registers_and_programmer_1_e_2,
       registers_and_programmer_1_e_4, registers_and_programmer_1_e_8;

  RAM_storage ram_storage_1 (
    .Bus(RAM_to_Bus), .Save(Write_to_RAM), .B_8(registers_and_programmer_1_b_8),
    .B_4(registers_and_programmer_1_b_4), .B_2(registers_and_programmer_1_b_2),
    .B_1(registers_and_programmer_1_b_1), .E_8(registers_and_programmer_1_e_8),
    .E_4(registers_and_programmer_1_e_4), .E_2(registers_and_programmer_1_e_2),
    .E_1(registers_and_programmer_1_e_1), .AR_1(address_register_1__1), .AR_2(address_register_1__2),
    .AR_4(address_register_1__4), .AR_8(address_register_1__8), .Bus_1(_1), .Bus_2(_2), .Bus_4(_4),
    .Bus_8(_8), .Out_1(ram_storage_1_out_1), .Out_2(ram_storage_1_out_2), .Out_4(ram_storage_1_out_4),
    .Out_8(ram_storage_1_out_8));
  Address_register address_register_1 (
    .Reset(Reset), .Read(Read_Addresses), .Clock(Clock), .Bus_8(_8), .Bus_4(_4), .Bus_2(_2), .Bus_1(_1),
    ._1(address_register_1__1), ._2(address_register_1__2), ._4(address_register_1__4),
    ._8(address_register_1__8));
  Registers_and_Programmer registers_and_programmer_1 (
    .Reset(Reset), .Clock(Clock), .Write(Start_Program), .Read_E(Read_Command),
    .Read_B(Read_Command_Argument), .D_8(address_register_1__8), .D_4(address_register_1__4),
    .D_2(address_register_1__2), .D_1(address_register_1__1), .Bus_8(_8), .Bus_4(_4), .Bus_2(_2), .Bus_1(_1),
    .E_8(registers_and_programmer_1_e_8), .E_4(registers_and_programmer_1_e_4),
    .E_2(registers_and_programmer_1_e_2), .E_1(registers_and_programmer_1_e_1),
    .B_8(registers_and_programmer_1_b_8), .B_4(registers_and_programmer_1_b_4),
    .B_2(registers_and_programmer_1_b_2), .B_1(registers_and_programmer_1_b_1));
  // Instructions instructions_1: pin names not known; wires that end beside it: ram_storage_1_out_8, ram_storage_1_out_4, ram_storage_1_out_2, ram_storage_1_out_1, instructions_1_p5, instructions_1_p6, A_M
  PullDown pulldown_1 (.out(A_M));
  PullDown pulldown_2 (.out(Read_Addresses));
  PullDown pulldown_3 (.out(RAM_to_Bus));
  PullDown pulldown_4 (.out(Write_to_RAM));
  PullDown pulldown_5 (.out(_8));
  PullDown pulldown_6 (.out(_4));
  PullDown pulldown_7 (.out(_2));
  PullDown pulldown_8 (.out(_1));
  PullDown pulldown_9 (.out(Flags));
  PullDown pulldown_10 (.out(APU_to_Bus));
  PullDown pulldown_11 (.out(Start_Program));
  APU apu_1 (
    .rA_8(register_1_out_8), .rA_4(register_1_out_4), .rA_2(register_1_out_2), .rA_1(register_1_out_1),
    .Reset(Reset), .Bus(APU_to_Bus), .Flags(Flags), .Clock(Clock), .Minus(Minus), .rB_8(register_2_out_8),
    .rB_4(register_2_out_4), .rB_2(register_2_out_2), .rB_1(register_2_out_1),
    .Flag_OverFlow(instructions_1_p6), .Flag_Negative(instructions_1_p5), .Bus_8(_8), .Bus_4(_4), .Bus_2(_2),
    .Bus_1(_1));
  register register_1 (
    ._8(_8), ._4(_4), ._2(_2), ._1(_1), .Reset(Reset), .Read(Write_to_rA), .Clock(Clock),
    .Out_8(register_1_out_8), .Out_4(register_1_out_4), .Out_2(register_1_out_2), .Out_1(register_1_out_1));
  tri_state_register tri_state_register_1 (
    ._8(_8), ._4(_4), ._2(_2), ._1(_1), .Reset(Reset), .Read(Write_to_rC), .Clock(Clock),
    .Write_to_bus(rC_to_Bus), .Out_8(_8), .Out_4(_4), .Out_2(_2), .Out_1(_1));
  PullDown pulldown_12 (.out(Read_Command_Argument));
  PullDown pulldown_13 (.out(Read_Command));
  PullDown pulldown_14 (.out(Write_to_rA));
  PullDown pulldown_15 (.out(Write_to_rB));
  PullDown pulldown_16 (.out(Write_to_rC));
  register register_2 (
    ._8(_8), ._4(_4), ._2(_2), ._1(_1), .Reset(Reset), .Read(Write_to_rB), .Clock(Clock),
    .Out_8(register_2_out_8), .Out_4(register_2_out_4), .Out_2(register_2_out_2), .Out_1(register_2_out_1));
  PullDown pulldown_17 (.out(Minus));
  PullDown pulldown_18 (.out(rC_to_Bus));
  PullDown pulldown_19 (.out(Reset));
  PullDown pulldown_20 (.out(Clock));

  // Notes on the sheet:
  //   A_M: Automatic/Manual instructions (automatically to load the asembly or to maually write it)
  //   Read_Command_Argument: Reads the argument/parameter from the bus line
  //   Read_Command: Reads what command to be ran from the bus line
  //   Write_to_rC: Register C starts to read from the bus line
  //   Write_to_rA: Register A starts to read from the bus line
  //   Write_to_rB: Register B starts to read from the bus line
  //   Flags: Enables Flags
  //   Read_Addresses: Pretty much self-explanatory. Enables the address registers to read from the BUS line.
  //   rC_to_Bus: Register C start to write to the bus line
endmodule
