// Digital circuit APU.dig as structural Verilog
module APU (
  input  rA_8,
  input  rA_4,
  input  rA_2,
  input  rA_1,
  input  Reset,
  input  Bus,
  input  Flags,
  input  Clock,
  input  Minus,
  input  rB_8,
  input  rB_4,
  input  rB_2,
  input  rB_1,
  output Flag_OverFlow,
  output Flag_Negative,
  output Bus_8,
  output Bus_4,
  output Bus_2,
  output Bus_1
);

  wire BUS_pin6, BUS_pin7, BUS_pin8, BUS_pin9, BUS_pin19, NOR_pin1, NOR_pin4, NOR_pin10, Register_pin13,
       SUM_pin1, SUM_pin3, SUM_pin4, SUM_pin5, SUM_pin10, SUM_pin12, SUM_pin13, SUM_pin14;

  _74283 SUM (
    .pin1(SUM_pin1), .pin2(1'b0), .pin3(SUM_pin3), .pin4(SUM_pin4), .pin5(SUM_pin5), .pin6(1'b0),
    .pin7(Minus), .pin8(1'b0), .pin10(SUM_pin10), .pin11(1'b0), .pin12(SUM_pin12), .pin13(SUM_pin13),
    .pin14(SUM_pin14), .pin15(1'b0), .pin16(1'b1));  // open: pin9
  _74245 u_BUS (
    .pin1(1'b1), .pin2(1'b0), .pin3(1'b0), .pin4(1'b0), .pin5(1'b0), .pin6(BUS_pin6), .pin7(BUS_pin7),
    .pin8(BUS_pin8), .pin9(BUS_pin9), .pin10(1'b0), .pin11(Bus_1), .pin12(Bus_2), .pin13(Bus_4),
    .pin14(Bus_8), .pin19(BUS_pin19), .pin20(1'b1));  // open: pin15, pin16, pin17, pin18
  _7486 XOR (
    .pin1(rB_1), .pin2(Minus), .pin3(SUM_pin5), .pin4(rB_2), .pin5(Minus), .pin6(SUM_pin3), .pin7(1'b0),
    .pin8(SUM_pin14), .pin9(rB_4), .pin10(Minus), .pin11(SUM_pin12), .pin12(rB_8), .pin13(Minus), .pin14(1'b1));
  _74283 SUM_2 (
    .pin1(BUS_pin8), .pin2(SUM_pin1), .pin3(rA_2), .pin4(BUS_pin9), .pin5(rA_1), .pin6(SUM_pin4),
    .pin7(1'b0), .pin8(1'b0), .pin10(BUS_pin6), .pin11(SUM_pin10), .pin12(rA_8), .pin13(BUS_pin7),
    .pin14(rA_4), .pin15(SUM_pin13), .pin16(1'b1));  // open: pin9
  LED led_1 (.in(BUS_pin7));
  LED led_2 (.in(BUS_pin6));
  LED led_3 (.in(BUS_pin8));
  LED led_4 (.in(BUS_pin9));
  _7402 NOR (
    .pin1(NOR_pin1), .pin2(BUS_pin9), .pin3(BUS_pin8), .pin4(NOR_pin4), .pin5(BUS_pin7), .pin6(BUS_pin6),
    .pin7(1'b0), .pin8(Flags), .pin9(1'b0), .pin10(NOR_pin10), .pin11(Bus), .pin12(1'b0), .pin13(BUS_pin19),
    .pin14(1'b1));
  _74173 Register (
    .pin1(1'b0), .pin2(1'b0), .pin3(Flag_OverFlow), .pin4(Flag_Negative), .pin7(Clock), .pin8(1'b0),
    .pin9(NOR_pin10), .pin10(NOR_pin10), .pin11(1'b0), .pin12(1'b0), .pin13(Register_pin13),
    .pin14(BUS_pin6), .pin15(Reset), .pin16(1'b1));  // open: pin5, pin6
  _7408 AND (
    .pin1(NOR_pin1), .pin2(NOR_pin4), .pin3(Register_pin13), .pin4(1'b0), .pin5(1'b0), .pin7(1'b0),
    .pin9(1'b0), .pin10(1'b0), .pin12(1'b0), .pin13(1'b0), .pin14(1'b1));  // open: pin6, pin8, pin11

  // Notes on the sheet:
  //   Third Board
  //   First Board
  //   Second Board
endmodule
