// Digital circuit Adder with Flags.dig as structural Verilog
module Adder_with_Flags (
  input  in_1,
  input  in_2,
  input  in_3,
  input  in_4,
  input  in_5,
  input  in_6,
  input  in_7,
  input  in_8,
  input  in_9,
  input  in_10,
  input  in_11,
  input  in_12,
  input  in_13,
  input  in_14,
  input  in_15,
  input  in_16,
  input  in_17,
  input  in_18
);

  wire _7402_1_pin1, _7402_1_pin4, _7402_1_pin10, _7408_1_pin3, _74173_1_pin3, _74173_1_pin4, _74245_1_pin6,
       _74245_1_pin7, _74245_1_pin8, _74245_1_pin9, _74245_1_pin11, _74245_1_pin12, _74245_1_pin13,
       _74245_1_pin14, _74245_1_pin19, _74283_1_pin2, _74283_1_pin3, _74283_1_pin5, _74283_1_pin6,
       _74283_1_pin11, _74283_1_pin12, _74283_1_pin14, _74283_1_pin15;

  _74245 _74245_1 (
    .pin1(1'b1), .pin2(1'b0), .pin3(1'b0), .pin4(1'b0), .pin5(1'b0), .pin6(_74245_1_pin6),
    .pin7(_74245_1_pin7), .pin8(_74245_1_pin8), .pin9(_74245_1_pin9), .pin10(1'b0), .pin11(_74245_1_pin11),
    .pin12(_74245_1_pin12), .pin13(_74245_1_pin13), .pin14(_74245_1_pin14), .pin19(_74245_1_pin19),
    .pin20(1'b1));  // open: pin15, pin16, pin17, pin18
  LED led_1 (.in(_74245_1_pin13));
  LED led_2 (.in(_74245_1_pin14));
  LED led_3 (.in(_74245_1_pin11));
  LED led_4 (.in(_74245_1_pin12));
  _74283 _74283_1 (
    .pin1(_74245_1_pin8), .pin2(_74283_1_pin2), .pin3(_74283_1_pin3), .pin4(_74245_1_pin9),
    .pin5(_74283_1_pin5), .pin6(_74283_1_pin6), .pin7(1'b0), .pin8(1'b0), .pin10(_74245_1_pin6),
    .pin11(_74283_1_pin11), .pin12(_74283_1_pin12), .pin13(_74245_1_pin7), .pin14(_74283_1_pin14),
    .pin15(_74283_1_pin15), .pin16(1'b1));  // open: pin9
  register register_1 (
    ._8(in_8), ._4(in_9), ._2(in_10), ._1(in_11), .Reset(in_12), .Read(in_13), .Clock(in_14),
    .Out_8(_74283_1_pin11), .Out_4(_74283_1_pin15), .Out_2(_74283_1_pin2), .Out_1(_74283_1_pin6));
  register register_2 (
    ._8(in_1), ._4(in_2), ._2(in_3), ._1(in_4), .Reset(in_5), .Read(in_6), .Clock(in_7),
    .Out_8(_74283_1_pin12), .Out_4(_74283_1_pin14), .Out_2(_74283_1_pin3), .Out_1(_74283_1_pin5));
  LED led_5 (.in(_74245_1_pin7));
  LED led_6 (.in(_74245_1_pin8));
  LED led_7 (.in(_74245_1_pin6));
  LED led_8 (.in(_74245_1_pin9));
  _7402 _7402_1 (
    .pin1(_7402_1_pin1), .pin2(_74245_1_pin9), .pin3(_74245_1_pin8), .pin4(_7402_1_pin4),
    .pin5(_74245_1_pin7), .pin6(_74245_1_pin6), .pin7(1'b0), .pin8(in_17), .pin9(1'b0),
    .pin10(_7402_1_pin10), .pin11(in_16), .pin12(1'b0), .pin13(_74245_1_pin19), .pin14(1'b1));
  _7408 _7408_1 (
    .pin1(_7402_1_pin1), .pin2(_7402_1_pin4), .pin3(_7408_1_pin3), .pin4(1'b0), .pin5(1'b0), .pin7(1'b0),
    .pin9(1'b0), .pin10(1'b0), .pin12(1'b0), .pin13(1'b0), .pin14(1'b1));  // open: pin6, pin8, pin11
  _74173 _74173_1 (
    .pin1(1'b0), .pin2(1'b0), .pin3(_74173_1_pin3), .pin4(_74173_1_pin4), .pin7(in_18), .pin8(1'b0),
    .pin9(_7402_1_pin10), .pin10(_7402_1_pin10), .pin11(1'b0), .pin12(1'b0), .pin13(_7408_1_pin3),
    .pin14(_74245_1_pin6), .pin15(in_15), .pin16(1'b1));  // open: pin5, pin6
  LED led_9 (.in(_74173_1_pin3));
  LED led_10 (.in(_74173_1_pin4));
endmodule
