// Digital circuit Address Register With Programmer.dig as structural Verilog
module Address_Register_With_Programmer (
  input  Reset,
  input  Read,
  input  Clock,
  input  Bus_8,
  input  Bus_4,
  input  Bus_2,
  input  Bus_1,
  input  Reset_2,
  input  Clock_2,
  input  Start_Program,
  input  D_8,
  input  D_4,
  input  D_2,
  input  D_1,
  input  Bus_8_2,
  input  Bus_4_2,
  input  Bus_2_2,
  input  Bus_1_2,
  input  Read_E,
  input  Read_B,
  output _1,
  output _2,
  output _4,
  output _8,
  output E_8,
  output E_4,
  output E_2,
  output E_1,
  output B_8,
  output B_4,
  output B_2,
  output B_1
);

  wire _7404_1_pin2, _7404_1_pin4, _7408_1_pin2, _7408_1_pin3, _7408_1_pin6, _7408_1_pin8, _7408_1_pin11,
       _7432_1_pin1, _7432_1_pin4, _7432_1_pin9, _7432_1_pin12, _74173_1_pin11, _74173_1_pin12,
       _74173_1_pin13, _74173_1_pin14, _74283_1_pin1, _74283_1_pin4, _74283_1_pin10, _74283_1_pin13;

  _74283 _74283_1 (
    .pin1(_74283_1_pin1), .pin2(1'b0), .pin3(_2), .pin4(_74283_1_pin4), .pin5(_1), .pin6(1'b1), .pin7(1'b0),
    .pin8(1'b0), .pin10(_74283_1_pin10), .pin11(1'b0), .pin12(_8), .pin13(_74283_1_pin13), .pin14(_4),
    .pin15(1'b0), .pin16(1'b1));  // open: pin9
  _7408 _7408_1 (
    .pin1(_74283_1_pin4), .pin2(_7408_1_pin2), .pin3(_7408_1_pin3), .pin4(_74283_1_pin1),
    .pin5(_7408_1_pin2), .pin6(_7408_1_pin6), .pin7(1'b0), .pin8(_7408_1_pin8), .pin9(_74283_1_pin13),
    .pin10(_7408_1_pin2), .pin11(_7408_1_pin11), .pin12(_74283_1_pin10), .pin13(_7408_1_pin2), .pin14(1'b1));
  _74173 _74173_1 (
    .pin1(1'b0), .pin2(1'b0), .pin3(_8), .pin4(_4), .pin5(_2), .pin6(_1), .pin7(Clock), .pin8(1'b0),
    .pin9(1'b0), .pin10(1'b0), .pin11(_74173_1_pin11), .pin12(_74173_1_pin12), .pin13(_74173_1_pin13),
    .pin14(_74173_1_pin14), .pin15(Reset), .pin16(1'b1));
  _7404 _7404_1 (
    .pin1(Read_E), .pin2(_7404_1_pin2), .pin3(Read_B), .pin4(_7404_1_pin4), .pin5(1'b0), .pin7(1'b0),
    .pin8(_7408_1_pin2), .pin9(Read), .pin11(1'b0), .pin13(1'b0), .pin14(1'b1));  // open: pin6, pin10, pin12
  _7432 _7432_1 (
    .pin1(_7432_1_pin1), .pin2(_7408_1_pin3), .pin3(_74173_1_pin14), .pin4(_7432_1_pin4),
    .pin5(_7408_1_pin6), .pin6(_74173_1_pin13), .pin7(1'b0), .pin8(_74173_1_pin12), .pin9(_7432_1_pin9),
    .pin10(_7408_1_pin8), .pin11(_74173_1_pin11), .pin12(_7432_1_pin12), .pin13(_7408_1_pin11), .pin14(1'b1));
  _74173 _74173_2 (
    .pin1(Start_Program), .pin2(Start_Program), .pin3(E_8), .pin4(E_4), .pin5(E_2), .pin6(E_1),
    .pin7(Clock_2), .pin8(1'b0), .pin9(_7404_1_pin2), .pin10(_7404_1_pin2), .pin11(Bus_1_2), .pin12(Bus_2_2),
    .pin13(Bus_4_2), .pin14(Bus_8_2), .pin15(Reset_2), .pin16(1'b1));
  _7408 _7408_2 (
    .pin1(Bus_1), .pin2(Read), .pin3(_7432_1_pin1), .pin4(Bus_2), .pin5(Read), .pin6(_7432_1_pin4),
    .pin7(1'b0), .pin8(_7432_1_pin9), .pin9(Bus_4), .pin10(Read), .pin11(_7432_1_pin12), .pin12(Bus_8),
    .pin13(Read), .pin14(1'b1));
  // Adapted_28C16A adapted_28c16a_1: pin names not known; wires that end beside it: 1'b1, 1'b0, 1'b0, 1'b0, 1'b0, 1'b0, 1'b0, 1'b0, 1'b1, D_8, 1'b0, D_4, Start_Program, D_2, E_8, D_1, E_4, B_1, E_2, B_2, B_4, 1'b0
  _74173 _74173_3 (
    .pin1(Start_Program), .pin2(Start_Program), .pin3(B_8), .pin4(B_4), .pin5(B_2), .pin6(B_1),
    .pin7(Clock_2), .pin8(1'b0), .pin9(_7404_1_pin4), .pin10(_7404_1_pin4), .pin11(Bus_1_2), .pin12(Bus_2_2),
    .pin13(Bus_4_2), .pin14(Bus_8_2), .pin15(Reset_2), .pin16(1'b1));

  // Notes on the sheet:
  //   Read_E: (Е) - Command
  //   Read_B: (B) - Command Arguments
  //   Upper Left Address Register (part 2)
  //   Lower Left Address Register (part 1)
  //   Upper Right Address Register (part 3)
  //   Programmer (Program)
  //   (Е) - Command/Instruction to be ran
  //   (B) - Command Argument
endmodule
