// Digital circuit Address register.dig as structural Verilog
module Address_register (
  input  Reset,
  input  Read,
  input  Clock,
  input  Bus_8,
  input  Bus_4,
  input  Bus_2,
  input  Bus_1,
  output _1,
  output _2,
  output _4,
  output _8
);

  wire _7404_1_pin8, _7408_1_pin1, _7408_1_pin3, _7408_1_pin4, _7408_1_pin6, _7408_1_pin8, _7408_1_pin9,
       _7408_1_pin11, _7408_1_pin12, _7432_1_pin1, _7432_1_pin4, _7432_1_pin9, _7432_1_pin12, _74173_1_pin11,
       _74173_1_pin12, _74173_1_pin13, _74173_1_pin14;

  _7404 _7404_1 (
    .pin1(1'b0), .pin3(1'b0), .pin5(1'b0), .pin7(1'b0), .pin8(_7404_1_pin8), .pin9(Read), .pin11(1'b0),
    .pin13(1'b0), .pin14(1'b1));  // open: pin2, pin4, pin6, pin10, pin12
  _7408 _7408_1 (
    .pin1(_7408_1_pin1), .pin2(_7404_1_pin8), .pin3(_7408_1_pin3), .pin4(_7408_1_pin4), .pin5(_7404_1_pin8),
    .pin6(_7408_1_pin6), .pin7(1'b0), .pin8(_7408_1_pin8), .pin9(_7408_1_pin9), .pin10(_7404_1_pin8),
    .pin11(_7408_1_pin11), .pin12(_7408_1_pin12), .pin13(_7404_1_pin8), .pin14(1'b1));
  _74283 _74283_1 (
    .pin1(_7408_1_pin4), .pin2(1'b0), .pin3(_2), .pin4(_7408_1_pin1), .pin5(_1), .pin6(1'b1), .pin7(1'b0),
    .pin8(1'b0), .pin10(_7408_1_pin12), .pin11(1'b0), .pin12(_8), .pin13(_7408_1_pin9), .pin14(_4),
    .pin15(1'b0), .pin16(1'b1));  // open: pin9
  _74173 _74173_1 (
    .pin1(1'b0), .pin2(1'b0), .pin3(_8), .pin4(_4), .pin5(_2), .pin6(_1), .pin7(Clock), .pin8(1'b0),
    .pin9(1'b0), .pin10(1'b0), .pin11(_74173_1_pin11), .pin12(_74173_1_pin12), .pin13(_74173_1_pin13),
    .pin14(_74173_1_pin14), .pin15(Reset), .pin16(1'b1));
  _7432 _7432_1 (
    .pin1(_7432_1_pin1), .pin2(_7408_1_pin3), .pin3(_74173_1_pin14), .pin4(_7432_1_pin4),
    .pin5(_7408_1_pin6), .pin6(_74173_1_pin13), .pin7(1'b0), .pin8(_74173_1_pin12), .pin9(_7432_1_pin9),
    .pin10(_7408_1_pin8), .pin11(_74173_1_pin11), .pin12(_7432_1_pin12), .pin13(_7408_1_pin11), .pin14(1'b1));
  _7408 _7408_2 (
    .pin1(Bus_1), .pin2(Read), .pin3(_7432_1_pin1), .pin4(Bus_2), .pin5(Read), .pin6(_7432_1_pin4),
    .pin7(1'b0), .pin8(_7432_1_pin9), .pin9(Bus_4), .pin10(Read), .pin11(_7432_1_pin12), .pin12(Bus_8),
    .pin13(Read), .pin14(1'b1));
endmodule
