// Digital circuit Instructions.dig as structural Verilog
module Instructions (
  input  Auto_Manual,
  input  A_5,
  input  A_4,
  input  A_3,
  input  A_2,
  input  A_1,
  input  A_0,
  output _1,
  output _2,
  output _3,
  output _4,
  output _5,
  output _6,
  output _7,
  output _8,
  output _9,
  output _10,
  output _11,
  output _12,
  output _13,
  output _14,
  output _15,
  output _16
);

  Adapted_28C16A_V2 adapted_28c16a_v2_1 (
    .A0(A_0), .A1(A_1), .A2(A_2), .A3(A_3), .nCE(Auto_Manual), .nOE(1'b1), .nWE(1'b0), .VCC(1'b1),
    .GND(1'b0), .I_O0(_1), .I_O1(_2), .I_O2(_3), .I_O3(_4), .I_O4(_5), .I_O5(_6), .I_O6(_7), .I_O7(_8),
    .A4(A_4), .A5(A_5));
  Adapted_28C16A_V2 adapted_28c16a_v2_2 (
    .A0(A_0), .A1(A_1), .A2(A_2), .A3(A_3), .nCE(Auto_Manual), .nOE(1'b1), .nWE(1'b0), .VCC(1'b1),
    .GND(1'b0), .I_O0(_9), .I_O1(_10), .I_O2(_11), .I_O3(_12), .I_O4(_13), .I_O5(_14), .I_O6(_15),
    .I_O7(_16), .A4(A_4), .A5(A_5));
endmodule
