// Digital circuit RAM(storage).dig as structural Verilog
module RAM_storage (
  input  Bus,
  input  Save,
  input  B_8,
  input  B_4,
  input  B_2,
  input  B_1,
  input  E_8,
  input  E_4,
  input  E_2,
  input  E_1,
  input  AR_1,
  input  AR_2,
  input  AR_4,
  input  AR_8,
  output Bus_1,
  output Bus_2,
  output Bus_4,
  output Bus_8,
  output Out_1,
  output Out_2,
  output Out_4,
  output Out_8
);

  wire NOT_2_pin4, NOT_2_pin6, NOT_2_pin8, NOT_2_pin10, NOT_2_pin12, RAM_2_pin5, RAM_2_pin7, RAM_2_pin9,
       RAM_2_pin11, RAM_pin3, RAM_pin5, RAM_pin7, RAM_pin9, RAM_pin11;

  _74189 RAM (
    .pin1(AR_1), .pin2(1'b0), .pin3(RAM_pin3), .pin4(E_1), .pin5(RAM_pin5), .pin6(E_2), .pin7(RAM_pin7),
    .pin8(1'b0), .pin9(RAM_pin9), .pin10(E_4), .pin11(RAM_pin11), .pin12(E_8), .pin13(AR_8), .pin14(AR_4),
    .pin15(AR_2), .pin16(1'b1));
  _7404 NOT (
    .pin1(1'b0), .pin3(RAM_pin7), .pin4(Out_2), .pin5(RAM_pin5), .pin6(Out_1), .pin7(1'b0), .pin8(RAM_pin3),
    .pin9(Save), .pin10(Out_8), .pin11(RAM_pin11), .pin12(Out_4), .pin13(RAM_pin9), .pin14(1'b1));  // open: pin2
  _74189 RAM_2 (
    .pin1(AR_1), .pin2(1'b0), .pin3(RAM_pin3), .pin4(B_1), .pin5(RAM_2_pin5), .pin6(B_2), .pin7(RAM_2_pin7),
    .pin8(1'b0), .pin9(RAM_2_pin9), .pin10(B_4), .pin11(RAM_2_pin11), .pin12(B_8), .pin13(AR_8),
    .pin14(AR_4), .pin15(AR_2), .pin16(1'b1));
  _7404 NOT_2 (
    .pin1(1'b0), .pin3(RAM_2_pin7), .pin4(NOT_2_pin4), .pin5(RAM_2_pin5), .pin6(NOT_2_pin6), .pin7(1'b0),
    .pin8(NOT_2_pin8), .pin9(Bus), .pin10(NOT_2_pin10), .pin11(RAM_2_pin11), .pin12(NOT_2_pin12),
    .pin13(RAM_2_pin9), .pin14(1'b1));  // open: pin2
  _74245 \_3_state__кранче  (
    .pin1(1'b1), .pin2(NOT_2_pin6), .pin3(NOT_2_pin4), .pin4(NOT_2_pin12), .pin5(NOT_2_pin10), .pin6(1'b0),
    .pin7(1'b0), .pin8(1'b0), .pin9(1'b0), .pin10(1'b0), .pin15(Bus_8), .pin16(Bus_4), .pin17(Bus_2),
    .pin18(Bus_1), .pin19(NOT_2_pin8), .pin20(1'b1));  // open: pin11, pin12, pin13, pin14
endmodule
