// Digital circuit Registers and Programmer.dig as structural Verilog
module Registers_and_Programmer (
  input  Reset,
  input  Clock,
  input  Write,
  input  Read_E,
  input  Read_B,
  input  D_8,
  input  D_4,
  input  D_2,
  input  D_1,
  input  Bus_8,
  input  Bus_4,
  input  Bus_2,
  input  Bus_1,
  output E_8,
  output E_4,
  output E_2,
  output E_1,
  output B_8,
  output B_4,
  output B_2,
  output B_1
);

  wire _7404_1_pin8, _7404_1_pin10;

  _7404 _7404_1 (
    .pin1(1'b0), .pin3(1'b0), .pin5(1'b0), .pin7(1'b0), .pin8(_7404_1_pin8), .pin9(Read_E),
    .pin10(_7404_1_pin10), .pin11(Read_B), .pin13(1'b0), .pin14(1'b1));  // open: pin2, pin4, pin6, pin12
  _74173 _74173_1 (
    .pin1(Write), .pin2(Write), .pin3(E_8), .pin4(E_4), .pin5(E_2), .pin6(E_1), .pin7(Clock), .pin8(1'b0),
    .pin9(_7404_1_pin8), .pin10(_7404_1_pin8), .pin11(Bus_1), .pin12(Bus_2), .pin13(Bus_4), .pin14(Bus_8),
    .pin15(Reset), .pin16(1'b1));
  // Adapted_28C16A adapted_28c16a_1: pin names not known; wires that end beside it: 1'b1, 1'b0, 1'b0, 1'b0, 1'b0, 1'b0, 1'b0, 1'b0, 1'b1, D_8, 1'b0, D_4, Write, D_2, E_8, D_1, E_4, B_1, E_2, B_2, B_4, 1'b0
  _74173 _74173_2 (
    .pin1(Write), .pin2(Write), .pin3(B_8), .pin4(B_4), .pin5(B_2), .pin6(B_1), .pin7(Clock), .pin8(1'b0),
    .pin9(_7404_1_pin10), .pin10(_7404_1_pin10), .pin11(Bus_1), .pin12(Bus_2), .pin13(Bus_4), .pin14(Bus_8),
    .pin15(Reset), .pin16(1'b1));
endmodule
