// Digital circuit Adapted 28C16A.dig as structural Verilog
// 16K (2K x 8) Parallel EEPROM;
// DATA Polling for End of Write Detection not implemented!
module Adapted_28C16A (
  input  A0,
  input  A1,
  input  A2,
  input  A3,
  input  nCE,
  input  nOE,
  input  nWE,
  input  VCC,
  input  GND,
  input  I_O0,
  input  I_O1,
  input  I_O2,
  input  I_O3,
  input  I_O4,
  input  I_O5,
  input  I_O6,
  input  I_O7
);

  EEPROM #(.AddrBits(4), .Bits(8)) eeprom_1 (
    .A({A3, A2, A1, A0}), .CS(nCE), .WE(nWE), .OE(nOE), .D({I_O7, I_O6, I_O5, I_O4, I_O3, I_O2, I_O1, I_O0}));
  PowerSupply powersupply_1 (.VDD(VCC), .GND(GND));

  // Notes on the sheet:
  //   A0: pin 8
  //   A1: pin 7
  //   A2: pin 6
  //   A3: pin 5
  //   nCE: pin 18, default 1
  //   nOE: pin 20, default 1
  //   nWE: pin 21, default 1
  //   VCC: pin 24, default 1
  //   GND: pin 12
  //   I_O0: pin 9
  //   I_O1: pin 10
  //   I_O2: pin 11
  //   I_O3: pin 13
  //   I_O4: pin 14
  //   I_O5: pin 15
  //   I_O6: pin 16
  //   I_O7: pin 17
  //   contents of eeprom_1 (hex, n*v repeats v):
  //   cd,23,40,c0,61,30,90,80,0,0,0,45,0,79
endmodule
