// Digital circuit adder(15).dig as structural Verilog
module adder_15 (
  input  in_1,
  input  in_2,
  input  in_3,
  input  in_4,
  input  in_5,
  input  in_6,
  input  in_7,
  input  in_8,
  input  in_9,
  input  in_10,
  input  in_11,
  input  in_12,
  input  in_13,
  input  in_14
);

  wire _74283_1_pin1, _74283_1_pin2, _74283_1_pin3, _74283_1_pin4, _74283_1_pin5, _74283_1_pin6,
       _74283_1_pin10, _74283_1_pin11, _74283_1_pin12, _74283_1_pin13, _74283_1_pin14, _74283_1_pin15;

  _74283 _74283_1 (
    .pin1(_74283_1_pin1), .pin2(_74283_1_pin2), .pin3(_74283_1_pin3), .pin4(_74283_1_pin4),
    .pin5(_74283_1_pin5), .pin6(_74283_1_pin6), .pin7(1'b0), .pin8(1'b0), .pin10(_74283_1_pin10),
    .pin11(_74283_1_pin11), .pin12(_74283_1_pin12), .pin13(_74283_1_pin13), .pin14(_74283_1_pin14),
    .pin15(_74283_1_pin15), .pin16(1'b1));  // open: pin9
  register register_B (
    ._8(in_11), ._4(in_10), ._2(in_9), ._1(in_8), .Reset(in_12), .Read(in_13), .Clock(in_14));  // open: Out_8, Out_4, Out_2, Out_1
  register register_A (
    ._8(in_4), ._4(in_3), ._2(in_2), ._1(in_1), .Reset(in_5), .Read(in_6), .Clock(in_7), .Out_1(_74283_1_pin5));  // open: Out_8, Out_4, Out_2
  LED led_1 (.in(_74283_1_pin10));
  LED led_2 (.in(_74283_1_pin13));
  LED led_3 (.in(_74283_1_pin1));
  LED led_4 (.in(_74283_1_pin4));
endmodule
