// Digital circuit full adder.dig as structural Verilog
module full_adder (
  input  _8,
  input  _4,
  input  _2,
  input  _1,
  input  Read,
  input  Clock,
  input  _8_2,
  input  _4_2,
  input  _2_2,
  input  _1_2,
  input  Read_2,
  input  Clock_2,
  input  Clear,
  input  Bus,
  input  Flags,
  input  Clock_3,
  input  Minus
);

  wire BUS_pin6, BUS_pin7, BUS_pin8, BUS_pin9, BUS_pin11, BUS_pin12, BUS_pin13, BUS_pin14, BUS_pin19,
       NOR_pin1, NOR_pin4, NOR_pin10, Register_3_pin3, Register_3_pin4, Register_3_pin13, SUM_2_pin3,
       SUM_2_pin5, SUM_2_pin12, SUM_2_pin14, SUM_pin1, SUM_pin3, SUM_pin4, SUM_pin5, SUM_pin10, SUM_pin12,
       SUM_pin13, SUM_pin14, XOR_pin1, XOR_pin4, XOR_pin9, XOR_pin12;

  _74283 SUM (
    .pin1(SUM_pin1), .pin2(1'b0), .pin3(SUM_pin3), .pin4(SUM_pin4), .pin5(SUM_pin5), .pin6(1'b0),
    .pin7(Minus), .pin8(1'b0), .pin10(SUM_pin10), .pin11(1'b0), .pin12(SUM_pin12), .pin13(SUM_pin13),
    .pin14(SUM_pin14), .pin15(1'b0), .pin16(1'b1));  // open: pin9
  _74245 u_BUS (
    .pin1(1'b1), .pin2(1'b0), .pin3(1'b0), .pin4(1'b0), .pin5(1'b0), .pin6(BUS_pin6), .pin7(BUS_pin7),
    .pin8(BUS_pin8), .pin9(BUS_pin9), .pin10(1'b0), .pin11(BUS_pin11), .pin12(BUS_pin12), .pin13(BUS_pin13),
    .pin14(BUS_pin14), .pin19(BUS_pin19), .pin20(1'b1));  // open: pin15, pin16, pin17, pin18
  LED led_1 (.in(BUS_pin13));
  LED led_2 (.in(BUS_pin14));
  LED led_3 (.in(BUS_pin11));
  LED led_4 (.in(BUS_pin12));
  _7486 XOR (
    .pin1(XOR_pin1), .pin2(Minus), .pin3(SUM_pin12), .pin4(XOR_pin4), .pin5(Minus), .pin6(SUM_pin14),
    .pin7(1'b0), .pin8(SUM_pin3), .pin9(XOR_pin9), .pin10(Minus), .pin11(SUM_pin5), .pin12(XOR_pin12),
    .pin13(Minus), .pin14(1'b1));
  _74283 SUM_2 (
    .pin1(BUS_pin8), .pin2(SUM_pin1), .pin3(SUM_2_pin3), .pin4(BUS_pin9), .pin5(SUM_2_pin5), .pin6(SUM_pin4),
    .pin7(1'b0), .pin8(1'b0), .pin10(BUS_pin6), .pin11(SUM_pin10), .pin12(SUM_2_pin12), .pin13(BUS_pin7),
    .pin14(SUM_2_pin14), .pin15(SUM_pin13), .pin16(1'b1));  // open: pin9
  register register_1 (
    ._8(_8), ._4(_4), ._2(_2), ._1(_1), .Reset(Clear), .Read(Read), .Clock(Clock), .Out_8(SUM_2_pin12),
    .Out_4(SUM_2_pin14), .Out_2(SUM_2_pin3), .Out_1(SUM_2_pin5));
  register register_2 (
    ._8(_8_2), ._4(_4_2), ._2(_2_2), ._1(_1_2), .Reset(Clear), .Read(Read_2), .Clock(Clock_2),
    .Out_8(XOR_pin1), .Out_4(XOR_pin4), .Out_2(XOR_pin9), .Out_1(XOR_pin12));
  LED led_5 (.in(BUS_pin7));
  LED led_6 (.in(BUS_pin6));
  LED led_7 (.in(BUS_pin8));
  LED led_8 (.in(BUS_pin9));
  _7402 NOR (
    .pin1(NOR_pin1), .pin2(BUS_pin9), .pin3(BUS_pin8), .pin4(NOR_pin4), .pin5(BUS_pin7), .pin6(BUS_pin6),
    .pin7(1'b0), .pin8(Flags), .pin9(1'b0), .pin10(NOR_pin10), .pin11(Bus), .pin12(1'b0), .pin13(BUS_pin19),
    .pin14(1'b1));
  _74173 Register_3 (
    .pin1(1'b0), .pin2(1'b0), .pin3(Register_3_pin3), .pin4(Register_3_pin4), .pin7(Clock_3), .pin8(1'b0),
    .pin9(NOR_pin10), .pin10(NOR_pin10), .pin11(1'b0), .pin12(1'b0), .pin13(Register_3_pin13),
    .pin14(BUS_pin6), .pin15(Clear), .pin16(1'b1));  // open: pin5, pin6
  _7408 AND (
    .pin1(NOR_pin1), .pin2(NOR_pin4), .pin3(Register_3_pin13), .pin4(1'b0), .pin5(1'b0), .pin7(1'b0),
    .pin9(1'b0), .pin10(1'b0), .pin12(1'b0), .pin13(1'b0), .pin14(1'b1));  // open: pin6, pin8, pin11
  LED led_9 (.in(Register_3_pin3));
  LED led_10 (.in(Register_3_pin4));

  // Notes on the sheet:
  //   Third Board
  //   First Board
  //   Second Board
endmodule
