// Digital circuit register.dig as structural Verilog
module register (
  input  _8,
  input  _4,
  input  _2,
  input  _1,
  input  Reset,
  input  Read,
  input  Clock,
  output Out_8,
  output Out_4,
  output Out_2,
  output Out_1
);

  wire _74173_1_pin9;

  _74173 _74173_1 (
    .pin1(1'b0), .pin2(1'b0), .pin3(Out_8), .pin4(Out_4), .pin5(Out_2), .pin6(Out_1), .pin7(Clock),
    .pin8(1'b0), .pin9(_74173_1_pin9), .pin10(_74173_1_pin9), .pin11(_1), .pin12(_2), .pin13(_4), .pin14(_8),
    .pin15(Reset), .pin16(1'b1));
  LED led_1 (.in(Out_8));
  LED led_2 (.in(Out_4));
  LED led_3 (.in(Out_2));
  LED led_4 (.in(Out_1));
  _7404 _7404_1 (
    .pin1(1'b0), .pin3(1'b0), .pin5(1'b0), .pin7(1'b0), .pin8(_74173_1_pin9), .pin9(Read), .pin11(1'b0),
    .pin13(1'b0), .pin14(1'b1));  // open: pin2, pin4, pin6, pin10, pin12
endmodule
